// Logisim project questao-2-a.circ as structural Verilog: 1 circuit, main circuit main
module main (
  input  a,
  input  b,
  input  c,
  output out_4
);

  wire ab_out, bc_out, ca_out;

  and ab (ab_out, a, a, b);
  and bc (bc_out, b, c);
  and ca (ca_out, a, c);
  or or_1 (out_4, ab_out, bc_out, bc_out, ca_out);
endmodule
