// Logisim project questao-2-b.circ as structural Verilog: 1 circuit, main circuit main
module main (
  input  a,
  input  b,
  input  c,
  output out_4
);

  wire a_nb_nc_out, abc_out, na_nbc_out, nab_nc_out, not_1_out, not_2_out, not_3_out, not_4_out, not_5_out;

  not not_1 (not_1_out, b);
  not not_2 (not_2_out, a);
  not not_3 (not_3_out, c);
  not not_4 (not_4_out, b);
  not not_5 (not_5_out, c);
  and na_nbc (na_nbc_out, not_2_out, not_1_out, c);
  and nab_nc (nab_nc_out, not_2_out, b, not_3_out);
  and a_nb_nc (a_nb_nc_out, a, not_4_out, not_5_out);
  and abc (abc_out, a, b, c);
  or or_1 (out_4, na_nbc_out, nab_nc_out, a_nb_nc_out, abc_out);
endmodule
