// Logisim project questao-3-parte1.circ as structural Verilog: 1 circuit, main circuit main
module main (
  input  a,
  input  b,
  input  c,
  output out_4
);

  wire ab_out, ac_out, bc_out;

  nand ab (ab_out, a, b);
  nand bc (bc_out, b, c);
  nand ac (ac_out, a, c);
  nand nand_1 (out_4, ab_out, bc_out, ac_out);
endmodule
