// Logisim project questao-3-parte2.circ as structural Verilog: 1 circuit, main circuit main
module main (
  input  a,
  input  b,
  input  c,
  output out_4
);

  wire nand_1_out, nand_2_out, nand_3_out, nand_4_out, nand_5_out, nand_6_out, nand_7_out;

  not nand_1 (nand_1_out, a);  // NAND_Gate
  not nand_2 (nand_2_out, b);  // NAND_Gate
  not nand_3 (nand_3_out, c);  // NAND_Gate
  nand nand_4 (nand_4_out, nand_1_out, c, nand_2_out, nand_2_out);
  nand nand_5 (nand_5_out, nand_1_out, b, nand_3_out);
  nand nand_6 (nand_6_out, a, nand_2_out, nand_2_out, nand_3_out);
  nand nand_7 (nand_7_out, a, b, c);
  nand nand_8 (out_4, nand_4_out, nand_5_out, nand_6_out, nand_7_out);
endmodule
