// Logisim project questao-4.circ as structural Verilog: 1 circuit, main circuit main
module main (
  input  S0,
  input  s1,
  input  d0,
  input  d1,
  input  d2,
  input  d3,
  output out_7
);

  wire nand_1_out, nand_2_out, nand_3_out, nand_4_out, nand_5_out, nand_6_out;

  not nand_1 (nand_1_out, S0);  // NAND_Gate
  not nand_2 (nand_2_out, s1);  // NAND_Gate
  nand nand_3 (nand_3_out, nand_1_out, nand_2_out, d0);
  nand nand_4 (nand_4_out, S0, nand_2_out, d1);
  nand nand_5 (nand_5_out, nand_1_out, s1, d2);
  nand nand_6 (nand_6_out, d3, s1, S0);
  nand nand_7 (out_7, nand_3_out, nand_4_out, nand_5_out, nand_6_out);
endmodule
